# Fritzing sketch SR04 (saved by Fritzing 1.0.0rc)
breadboards: 1

parts:
  HC-SR04_Sensor_1 = HC-SR04 Ultrasonic Distance Sensor
  Part1 = Arduino Uno (Rev3) - ICSP

nets:
  VCC: HC-SR04_Sensor_1.VCC, Part1.5V
  N1: HC-SR04_Sensor_1.TRIG, Part1.D7
  N2: HC-SR04_Sensor_1.ECHO, Part1.D8
  GND: HC-SR04_Sensor_1.GND, Part1.GND
